// Digital circuit PC.dig as structural Verilog
module PC (
  input  [31:0] ALU,
  input  C,
  input  abs,
  input  rel,
  output [31:0] Next,
  output [31:0] PC
);

  wire Reset_out;
  wire [31:0] Add_ALU_s, multiplexer_1_out, multiplexer_2_out;
  wire [31:16] undriven;

  Register #(.Bits(32), .isProgramCounter("true")) u_PC (.D(multiplexer_2_out), .C(~C), .en(Reset_out), .Q(PC));
  Reset Reset (.out(Reset_out));
  Add #(.Bits(32)) Add_One (.a(PC), .b({undriven, 16'h1}), .c_i(1'b0), .s(Next));  // open: c_o
  Add #(.Bits(32)) Add_ALU (.a(Next), .b(ALU), .c_i(1'b0), .s(Add_ALU_s));  // open: c_o
  Multiplexer #(.Bits(32)) multiplexer_1 (.sel(rel), .in_0(Next), .in_1(Add_ALU_s), .out(multiplexer_1_out));
  Multiplexer #(.Bits(32)) multiplexer_2 (.sel(abs), .in_0(multiplexer_1_out), .in_1(ALU), .out(multiplexer_2_out));
  // Pins of 16 and 32 bits meet at {undriven, 16'h1}

  // Notes on the sheet:
  //   ALU: La salida actual de la ALU, este valor se usa como dirección en caso de un salto o se suma a la dirección actual
  //   Next: Dirección de la siguiente instrucción a ejecutar. Puede ser utilizado como una dirección de retorno.
  //   PC: El contador de programa actual
  //   abs: Provoca un salto absoluto. El valor de la entrada de la ALU se utiliza como la nueva dirección
  //   rel: Se activa si hay un salto relativo. El valor de la entrada de la ALU se le suma a la dirección actual
endmodule
